# Fritzing sketch Nachlaufschaltung (saved by Fritzing 0.9.3b)
breadboards: 1

parts:
  U1 = 555 Timer [package="SO8 [SMD]"]  # not connected
  D1 = Rectifier Diode [part_number=1N4001 package="Melf DO-213 AB [SMD]"]
  2N3055 = npn-Powertransistor [package="TO220 [THT]"]
  R1 = Resistor [tolerance=±5% resistance=1k package="1206 [SMD]"]
  R2 = Resistor [tolerance=±5% resistance=100 package="2010 [SMD]"]
  R3 = Resistor [tolerance=±5% resistance=100k package="2010 [SMD]"]
  R4 = Resistor [tolerance=±5% resistance=330 package="2010 [SMD]"]
  S1 = Pushbutton [package="[THT]"]
  C2 = Electrolytic Capacitor [capacitance=10μF package="0605 [SMD, electrolytic]"]
  JACK1 = 2.1mm Barrel Jack with Terminal Block
  BULB2 = Incandescent light bulb small [package="bulb sm"]

nets:
  N1: D1.cathode, R1.Pin_0, S1.Pin_1, S1.Pin_2
  N2: D1.anode, R2.Pin_0
  N3: 2N3055.base, R4.Pin_1
  N4: 2N3055.collector, BULB2.1
  N5: 2N3055.emitter, S1.Pin_3, S1.Pin_4, C2.+
  N6: R1.Pin_1, R3.Pin_1, JACK1.POS, BULB2.2
  N7: R2.Pin_1, R3.Pin_0, C2.-

notes:
  12V/9V
